# Fritzing sketch jetson_finder_schmetics_lcd_screen (saved by Fritzing 0.9.4)
breadboards: 1

parts:
  Jetson_Nano2 = Jetson Nano
  LCD1 = LCD screen
  R1 = Rotary Potentiometer (Small) [maximum_resistance=100kΩ package=THT]
  LED1 = LED - 5mm [color="Red (633nm)" package="5 mm [THT]"]
  LED2 = LED - 5mm [color="Red (633nm)" package="5 mm [THT]"]
  R2 = Resistor [tolerance=±5% resistance=220 package=THT]
  R3 = Resistor [tolerance=±5% resistance=220 package=THT]
  R4 = Resistor [tolerance=±5% resistance=220 package=THT]

nets:
  N1: Jetson_Nano2.GPIO11, R3.Pin_0
  N2: Jetson_Nano2.GPIO19, LCD1.VSS, LCD1.R/W, LCD1.LED-, R1.leg1, LED1.cathode, LED2.cathode
  N3: Jetson_Nano2.GPIO26, LCD1.VDD, R1.leg2, R4.Pin_1
  N4: Jetson_Nano2.ID_SC, R2.Pin_0
  N5: Jetson_Nano2.GPIO25, LCD1.RS
  N6: Jetson_Nano2.GND, LCD1.E, LCD1.DB7
  N7: Jetson_Nano2.GPIO18, LCD1.DB4
  N8: Jetson_Nano2.GPIO15, LCD1.DB5
  N9: Jetson_Nano2.GPIO14, LCD1.DB6
  N10: LCD1.V0, R1.wiper
  N11: LCD1.LED+, R4.Pin_0
  N12: LED1.anode, R3.Pin_1
  N13: LED2.anode, R2.Pin_1
